# Fritzing sketch fixmix_circuit_diagramm (saved by Fritzing 0.9.3b)
breadboards: 1

parts:
  Raspberry_Pi_1 = Raspberry Pi 3 [part_number=RPI-3-V1.2]
  M1 = DC Motor
  M2 = DC Motor
  M3 = DC Motor
  M4 = DC Motor  # not connected
  M5 = DC Motor  # not connected
  M6 = DC Motor
  D1 = Diode [package=diode-1n4001]
  D2 = Diode [package=diode-1n4001]
  D3 = Diode [package=diode-1n4001]  # not connected
  D4 = Diode [package=diode-1n4001]
  D5 = Diode [package=diode-1n4001]
  D6 = Diode [package=diode-1n4001]
  Power_plug1 = Power plug
  Power_plug2 = Power plug
  8_Channel_Relay1 = 8 Channel Power Relay
  Part1 = OLED Monochrome 128x64 0.96 inch [part_number=326]
  S1 = Round Pushbutton
  S2 = Round Pushbutton
  U2 = V_REG_MIC2920 [package=sot223]
  Part2 = NeoPixel Stick [part_number=1426]

nets:
  3V3: Raspberry_Pi_1.3v3, Raspberry_Pi_1.3V3, 8_Channel_Relay1.VCC, Part1.VIN
  GND: Raspberry_Pi_1.GND, Raspberry_Pi_1.GIPO6, 8_Channel_Relay1.GND, Part1.GND, S1.leg0, S2.leg0, U2.OUT, Part2.GND
  N1: Raspberry_Pi_1.GIPO17, 8_Channel_Relay1.IN1
  N2: Raspberry_Pi_1.GIPO27, 8_Channel_Relay1.IN2
  N3: Raspberry_Pi_1.GIPO22, 8_Channel_Relay1.IN3
  N4: Raspberry_Pi_1.GIPO10, Part1.MOSI_SDA
  N5: Raspberry_Pi_1.GIPO11, Part1.SCLK_SCK
  N6: Raspberry_Pi_1.GIPO5, S2.leg1
  N7: Raspberry_Pi_1.GIPO13, S1.leg1
  N8: Raspberry_Pi_1.GIPO26, Part2.DATAIN
  N9: Raspberry_Pi_1.GIPO8, Part1.CS
  N10: Raspberry_Pi_1.GIPO25, 8_Channel_Relay1.IN6
  N11: Raspberry_Pi_1.GIPO24, 8_Channel_Relay1.IN5
  N12: Raspberry_Pi_1.GIPO23, 8_Channel_Relay1.IN4
  N13: Raspberry_Pi_1.GIPO15, Part1.DC_SA0
  N14: Raspberry_Pi_1.GIPO14, Part1.RESET
  N15: M1.pin_1, 8_Channel_Relay1.COM#22
  N16: M2.pin_1, 8_Channel_Relay1.COM#25
  N17: M3.pin_1, 8_Channel_Relay1.COM#28
  N18: M3.pin_2, D1.C, D2.C, D4.C, D5.C, D6.C, Power_plug1.VCC
  N19: M6.pin_2, 8_Channel_Relay1.COM#37
  N20: D4.A, 8_Channel_Relay1.COM#31
  N21: D5.A, 8_Channel_Relay1.COM#34
  N22: Power_plug1.GND, 8_Channel_Relay1.NO
  N23: Power_plug2.VCC, U2.IN
  GND_2: Power_plug2.GND, U2.GND

notes:
  Three motors are wired to run clockwise andthe other three are wired to run counter-clockwise
  12v Switching Power Supply has two outputs
  5v Regulator
  "Flyback" diodes prevent current from traveling backwards through the system when turned off
  A breadboard is used as our power distrobution board.
  Using a NeoPixel LED model for the Dotstar strip. Dotstar LEDs also have a CI pin that I'll label. We used 45 pixels on our bartender
  CI ^
  Relays run with 5v power, but are controlled with 3.3v logic
  Left Btn
  Right Btn
  Input
  Output
  Raspberry Pi 3 (Could also be a Raspberry Pi Zero)
  Smart Bartender Schematic

custom parts:
  8 Channel Power Relay: An 8 channel power relay. The module operates at 5V.
  OLED Monochrome 128x64 0.96 inch: These displays are small, only about 1" diameter, but very readable due to the high contrast of an OLED display. This display is made of 128x64 individual white OLED pixels, each one is turned on or off by the controller chip. Because the display makes its own light, no backlight is required. This reduces the power required to run the OLED and is why the display has such high contrast; we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
  NeoPixel Stick: Make your own little LED strip arrangement with this stick of NeoPixel LEDs. We crammed 8 of the tiny 5050 (5mm x 5mm) smart RGB LEDs onto a PCB with mounting holes and a chainable design. Use only one microcontroller pin to control as many as you can chain together! Each LED is addressable as the driver chip is inside the LED. Each one has ~18mA constant current drive so the color will be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
